# Fritzing sketch cmcnul3project (saved by Fritzing 0.9.3b)
breadboards: 1

parts:
  Part1 = Arduino Uno (Rev3) - ICSP
  LCD1 = LCD screen
  S1 = Pushbutton [package="[THT]"]
  S2 = Pushbutton [package="[THT]"]
  S3 = Pushbutton [package="[THT]"]
  LED3 = LED - 3mm [color="Green (555nm)" package="3 mm [THT]"]
  R3 = Resistor [tolerance=±5% resistance=1k package="2010 [SMD]"]
  R4 = Resistor [tolerance=±5% resistance=1k package="2010 [SMD]"]
  R5 = Resistor [tolerance=±5% resistance=1k package="2010 [SMD]"]
  R7 = Trimmer Potentiometer [maximum_resistance=10kΩ package=THT]
  R8 = Resistor [tolerance=±5% resistance=220 package=THT]
  R10 = Resistor [tolerance=±5% resistance=220 package=THT]
  R11 = Resistor [tolerance=±5% resistance=220 package=THT]
  LED4 = LED - 3mm [color="Red (633nm)" package="3 mm [THT]"]

nets:
  N1: Part1.ICSP_MOSI, Part1.D11_PWM/MOSI, LCD1.E
  5V: Part1.5V, LCD1.VDD, S1.Pin_1, S1.Pin_2, S2.Pin_1, S2.Pin_2, S3.Pin_1, S3.Pin_2, R7.leg2, R8.Pin_1
  N2: Part1.D9_PWM, S3.Pin_3, S3.Pin_4, R5.Pin_0
  N3: Part1.D10_PWM/SS, S2.Pin_3, S2.Pin_4, R4.Pin_0
  N4: Part1.D12/MISO, LCD1.RS
  N5: Part1.D13/SCK, S1.Pin_3, S1.Pin_4, R3.Pin_0
  N6: Part1.D2, LED3.anode
  N7: Part1.D3_PWM, LED4.anode
  N8: Part1.D4, LCD1.DB4
  N9: Part1.D5_PWM, LCD1.DB5
  N10: Part1.D6_PWM, LCD1.DB6
  N11: Part1.D7, LCD1.DB7
  GND: Part1.GND, LCD1.VSS, LCD1.R/W, LCD1.LED-, R3.Pin_1, R4.Pin_1, R5.Pin_1, R7.leg1, R10.Pin_1, R11.Pin_1
  N12: LCD1.V0, R7.wiper
  N13: LCD1.LED+, R8.Pin_0
  N14: LED3.cathode, R10.Pin_0
  N15: R11.Pin_0, LED4.cathode
